# Fritzing sketch schematic (saved by Fritzing 0.8.7b)
breadboards: 1

parts:
  R1_-_For_LED = Resistor [tolerance=±5% resistance=220 package=THT]
  R2_-_For_Photoresistor = Resistor [tolerance=±5% resistance=220 package=THT]
  LED1 = LED - 5mm [color="Red (633nm)" package="5 mm [THT]"]
  R3_-_Photoresistor = Photocell (LDR) [package=THT]
  Arduino1 = Arduino Uno (Rev3)

nets (from the breadboard view):
  N1: R1_-_For_LED.Pin_0, LED1.anode
  N2: R1_-_For_LED.Pin_1, Arduino1.D9_PWM
  N3: R2_-_For_Photoresistor.Pin_1, R3_-_Photoresistor.pin_0, Arduino1.A0
  N4: LED1.cathode, R3_-_Photoresistor.pin_1, Arduino1.GND
