# Fritzing sketch schematic (saved by Fritzing 0.7.4b)
breadboards: 1

parts:
  Arduino1 = Arduino
  LED1 = RGB LED (com. anode, rbg) [package="5 mm [THT]"]
  R1 = Photocell (LDR) [package=THT]
  R2 = Resistor [tolerance=±5% resistance=220 package=THT]
  R3 = Resistor [tolerance=±5% resistance=220 package=THT]
  R4 = Resistor [tolerance=±5% resistance=220 package=THT]
  R5 = Resistor [tolerance=±5% resistance=220 package=THT]

nets:
  N1: Arduino1.D11, R3.Pin_1
  N2: Arduino1.D10, R5.Pin_1
  N3: Arduino1.D9, R4.Pin_1
  N4: Arduino1.+5V, R2.Pin_0
  N5: Arduino1.GND, R1.pin_1
  N6: Arduino1.A0, R1.pin_0, R2.Pin_1
  N7: LED1.red_cathode, R3.Pin_0
  N8: LED1.blue_cathode, R4.Pin_0
  N9: LED1.green_cathode, R5.Pin_0
